# Fritzing sketch Board (saved by Fritzing 0.9.2b)
circuit board: 13.9445cm x 8.39482cm
breadboards: 3

parts:
  Part1 = Arduino Due (Rev2b)
  Q1 = PNP-Transistor [package="TO92 [THT]"]
  Q2 = PNP-Transistor [package="TO92 [THT]"]
  VCC1 = Battery
  7_Segment3 = 7 Segment Display
  7_Segment4 = 7 Segment Display
  R1 = Resistor [tolerance=±5% resistance=100 package=THT]
  R2 = Resistor [tolerance=±5% resistance=100 package=THT]
  Q3 = PNP-Transistor [package="TO92 [THT]"]
  Q4 = PNP-Transistor [package="TO92 [THT]"]
  Q5 = PNP-Transistor [package="TO92 [THT]"]
  Q6 = PNP-Transistor [package="TO92 [THT]"]
  Q7 = PNP-Transistor [package="TO92 [THT]"]
  R3 = Resistor [tolerance=±5% resistance=100 package=THT]
  R4 = Resistor [tolerance=±5% resistance=100 package=THT]
  R5 = Resistor [tolerance=±5% resistance=100 package=THT]
  R6 = Resistor [tolerance=±5% resistance=100 package=THT]
  R7 = Resistor [tolerance=±5% resistance=100 package=THT]
  R8 = Resistor [tolerance=±5% resistance=120 package=THT]
  R9 = Resistor [tolerance=±5% resistance=120 package=THT]
  R10 = Resistor [tolerance=±5% resistance=120 package=THT]
  R11 = Resistor [tolerance=±5% resistance=120 package=THT]
  R12 = Resistor [tolerance=±5% resistance=120 package=THT]
  R13 = Resistor [tolerance=±5% resistance=120 package=THT]
  R14 = Resistor [tolerance=±5% resistance=120 package=THT]
  Q8 = PNP-Transistor [package="TO92 [THT]"]
  Q9 = PNP-Transistor [package="TO92 [THT]"]
  Q10 = PNP-Transistor [package="TO92 [THT]"]
  Q11 = PNP-Transistor [package="TO92 [THT]"]
  Q12 = PNP-Transistor [package="TO92 [THT]"]
  Q13 = PNP-Transistor [package="TO92 [THT]"]
  Q14 = PNP-Transistor [package="TO92 [THT]"]
  Q15 = PNP-Transistor [package="TO92 [THT]"]
  Q16 = PNP-Transistor [package="TO92 [THT]"]
  Q17 = PNP-Transistor [package="TO92 [THT]"]
  Q18 = PNP-Transistor [package="TO92 [THT]"]
  Q19 = PNP-Transistor [package="TO92 [THT]"]
  Q20 = PNP-Transistor [package="TO92 [THT]"]
  Q21 = PNP-Transistor [package="TO92 [THT]"]
  Q22 = PNP-Transistor [package="TO92 [THT]"]
  R15 = Resistor [tolerance=±5% resistance=120 package=THT]
  R16 = Resistor [tolerance=±5% resistance=120 package=THT]
  R17 = Resistor [tolerance=±5% resistance=120 package=THT]
  R18 = Resistor [tolerance=±5% resistance=120 package=THT]
  R19 = Resistor [tolerance=±5% resistance=120 package=THT]
  R20 = Resistor [tolerance=±5% resistance=120 package=THT]
  R21 = Resistor [tolerance=±5% resistance=120 package=THT]
  R22 = Resistor [tolerance=±5% resistance=120 package=THT]
  R23 = Resistor [tolerance=±5% resistance=120 package=THT]
  R24 = Resistor [tolerance=±5% resistance=120 package=THT]
  R25 = Resistor [tolerance=±5% resistance=120 package=THT]
  R26 = Resistor [tolerance=±5% resistance=120 package=THT]
  R27 = Resistor [tolerance=±5% resistance=120 package=THT]
  R28 = Resistor [tolerance=±5% resistance=120 package=THT]
  R29 = Resistor [tolerance=±5% resistance=120 package=THT]
  R30 = Resistor [tolerance=±5% resistance=100 package=THT]
  R31 = Resistor [tolerance=±5% resistance=100 package=THT]
  R32 = Resistor [tolerance=±5% resistance=100 package=THT]
  R33 = Resistor [tolerance=±5% resistance=100 package=THT]
  R34 = Resistor [tolerance=±5% resistance=100 package=THT]
  R35 = Resistor [tolerance=±5% resistance=100 package=THT]
  R36 = Resistor [tolerance=±5% resistance=100 package=THT]
  R37 = Resistor [tolerance=±5% resistance=100 package=THT]
  R38 = Resistor [tolerance=±5% resistance=100 package=THT]
  R39 = Resistor [tolerance=±5% resistance=100 package=THT]
  R40 = Resistor [tolerance=±5% resistance=100 package=THT]
  R41 = Resistor [tolerance=±5% resistance=100 package=THT]
  R42 = Resistor [tolerance=±5% resistance=100 package=THT]
  R43 = Resistor [tolerance=±5% resistance=100 package=THT]
  R44 = Resistor [tolerance=±5% resistance=100 package=THT]
  S1 = Pushbutton [package="[THT]"]
  R45 = Resistor [tolerance=±5% resistance=10k package=THT]
  J1 = male pin header, 7 pins [form="♂ (male)"]
  R49 = Resistor [tolerance=±5% resistance=10k package=THT]
  R50 = Resistor [tolerance=±5% resistance=10k package=THT]
  R51fritzing_straight_7_pin_header = Resistor [tolerance=±5% resistance=10k package=THT]
  R52 = Resistor [tolerance=±5% resistance=10k package=THT]
  7_Segment1 = 7 Segment Display
  J2 = male pin header, 2 pins [form="♂ (male)"]
  J3 = male pin header, 9 pins [form="♂ (male)"]
  J4 = male pin header, 9 pins [form="♂ (male)"]
  J6 = male pin header, 2 pins [form="♂ (male)"]
  J7 = male pin header, 9 pins [form="♂ (male)"]

nets:
  N1: Part1.D18/TX1, R23.Pin_1
  N2: Part1.D19/RX1, R24.Pin_1
  N3: Part1.D21/SCL3, R25.Pin_1
  N4: Part1.GND, Q1.E, Q2.E, VCC1.-, Q3.E, Q4.E, Q5.E, Q6.E, Q7.E, Q8.E, Q9.E, Q10.E, Q11.E, Q12.E, Q13.E, Q14.E, Q15.E, Q16.E, Q17.E, Q18.E, Q19.E, Q20.E, Q21.E, Q22.E, R45.Pin_1, J1.pin1, R49.Pin_1, R50.Pin_1, R51fritzing_straight_7_pin_header.Pin_1, R52.Pin_1, J2.pin1
  N5: Part1.VIN, VCC1.+, 7_Segment3.common_anode, 7_Segment3.Segment_B, 7_Segment4.common_anode, R7.Pin_1, R39.Pin_1, 7_Segment1.Segment_F, 7_Segment1.common_anode, J2.pin2, J3.pin1, J3.pin5, J4.pin5, J7.pin4, J7.pin5
  N6: Part1.D2_PWM, R8.Pin_1
  N7: Part1.D3_PWM, R9.Pin_1
  N8: Part1.D5_PWM, R11.Pin_1
  N9: Part1.D6_PWM, R10.Pin_1
  N10: Part1.D7_PWM, R12.Pin_1
  N11: Part1.5V, R17.Pin_1, S1.Pin_1, S1.Pin_2, J1.pin2, J6.pin1
  N12: Part1.D22, R26.Pin_1
  N13: Part1.D24, R27.Pin_1
  N14: Part1.D26, R28.Pin_1
  N15: Part1.D28, R29.Pin_1
  N16: Part1.D32, R15.Pin_1
  N17: Part1.D34, R16.Pin_1
  N18: Part1.D38, R18.Pin_1
  N19: Part1.D40, R19.Pin_1
  N20: Part1.D42, R20.Pin_1
  N21: Part1.D44, R21.Pin_1
  N22: Part1.D46, R22.Pin_1
  N23: Part1.D47, J1.pin6, R49.Pin_0
  N24: Part1.D48, R13.Pin_1
  N25: Part1.D49, J1.pin5, R52.Pin_0
  N26: Part1.D50, R14.Pin_1
  N27: Part1.D51, J1.pin4, R51fritzing_straight_7_pin_header.Pin_0
  N28: Part1.D52, S1.Pin_4, R45.Pin_0, J6.pin2
  N29: Part1.D53, J1.pin3, R50.Pin_0
  N30: Q1.B, R8.Pin_0
  N31: Q1.C, R1.Pin_0
  N32: Q2.B, R9.Pin_0
  N33: Q2.C, R2.Pin_0
  N34: 7_Segment3.Segment_G, R43.Pin_1, J7.pin8
  N35: 7_Segment3.Segment_F, R42.Pin_1, J7.pin9
  N36: 7_Segment3.Segment_E, R41.Pin_1, J7.pin7
  N37: 7_Segment3.Segment_D, R40.Pin_1, J7.pin3
  N38: 7_Segment3.Segment_DP, 7_Segment3.Segment_C, R44.Pin_1, J7.pin2
  N39: 7_Segment3.Segment_A, R38.Pin_1, J7.pin6
  N40: 7_Segment4.Segment_G, R36.Pin_1, J4.pin2
  N41: 7_Segment4.Segment_F, R35.Pin_1, J4.pin1
  N42: 7_Segment4.Segment_E, R34.Pin_1, J4.pin3
  N43: 7_Segment4.Segment_D, R33.Pin_1, J4.pin7
  N44: 7_Segment4.Segment_DP, R37.Pin_1, J4.pin8
  N45: 7_Segment4.Segment_C, R32.Pin_1, J4.pin9
  N46: 7_Segment4.Segment_B, R31.Pin_1, J4.pin6
  N47: 7_Segment4.Segment_A, R30.Pin_1, J4.pin4
  N48: R1.Pin_1, 7_Segment1.Segment_A, J3.pin4
  N49: R2.Pin_1, 7_Segment1.Segment_B, J3.pin6
  N50: Q3.B, R11.Pin_0
  N51: Q3.C, R3.Pin_0
  N52: Q4.B, R10.Pin_0
  N53: Q4.C, R4.Pin_0
  N54: Q5.B, R14.Pin_0
  N55: Q5.C, R5.Pin_0
  N56: Q6.B, R12.Pin_0
  N57: Q6.C, R7.Pin_0
  N58: Q7.B, R13.Pin_0
  N59: Q7.C, R6.Pin_0
  N60: R3.Pin_1, 7_Segment1.Segment_D, J3.pin7
  N61: R4.Pin_1, 7_Segment1.Segment_E, J3.pin3
  N62: R5.Pin_1, 7_Segment1.Segment_DP, J3.pin8
  N63: R6.Pin_1, 7_Segment1.Segment_G, J3.pin2
  N64: Q8.B, R15.Pin_0
  N65: Q8.C, R30.Pin_0
  N66: Q9.B, R16.Pin_0
  N67: Q9.C, R31.Pin_0
  N68: Q10.B, R17.Pin_0
  N69: Q10.C, R32.Pin_0
  N70: Q11.B, R18.Pin_0
  N71: Q11.C, R33.Pin_0
  N72: Q12.B, R19.Pin_0
  N73: Q12.C, R34.Pin_0
  N74: Q13.B, R20.Pin_0
  N75: Q13.C, R35.Pin_0
  N76: Q14.B, R21.Pin_0
  N77: Q14.C, R36.Pin_0
  N78: Q15.B, R22.Pin_0
  N79: Q15.C, R37.Pin_0
  N80: Q16.B, R23.Pin_0
  N81: Q16.C, R38.Pin_0
  N82: Q17.B, R24.Pin_0
  N83: Q17.C, R39.Pin_0
  N84: Q18.B, R25.Pin_0
  N85: Q18.C, R40.Pin_0
  N86: Q19.B, R26.Pin_0
  N87: Q19.C, R41.Pin_0
  N88: Q20.B, R27.Pin_0
  N89: Q20.C, R42.Pin_0
  N90: Q21.B, R28.Pin_0
  N91: Q21.C, R43.Pin_0
  N92: Q22.B, R29.Pin_0
  N93: Q22.C, R44.Pin_0

notes:
  rhu@seas.upenn.edu
